# Fritzing sketch proto1 (saved by Fritzing 0.9.3b)
breadboards: 1

parts:
  D1 = Rectifier Diode [part_number=1N4001 package="300 mil [THT]"]
  S1 = Pushbutton [package="[THT]"]
  R1 = Resistor [tolerance=±5% resistance=10k package=THT]
  Part1 = Arduino Uno (Rev3)
  Q1 = Basic FET N-Channel [part_number=IRF520 package="TO220 [THT]"]
  L1 = Solenoid
  Power_plug1 = Power plug

nets:
  N1: D1.cathode, L1.pin2, Power_plug1.VCC
  N2: D1.anode, Q1.drain, L1.pin1
  N3: S1.Pin_1, S1.Pin_2, R1.Pin_0, Part1.D2
  N4: S1.Pin_3, S1.Pin_4, Part1.5V
  GND: R1.Pin_1, Part1.GND, Q1.source, Power_plug1.GND
  N5: Part1.D9_PWM, Q1.gate

notes:
  12V
